// Logisim project 21236277.circ as structural Verilog: 3 circuits, main circuit RockPaperLizardSpock
module RockPaperLizardSpock (
  input  A1,
  input  A0,
  input  B1,
  input  B0,
  output W1,
  output W0
);

  wire LEDControl_a_wins, LEDControl_b_wins;

  RPLS RPLS (.A1(A1), .A0(A0), .B1(B1), .B0(B0), .W1(W1), .W0(W0));
  LEDControl LEDControl (.W1(W1), .W0(W0), .A_Wins(LEDControl_a_wins), .B_Wins(LEDControl_b_wins));
  LED A_Wins (.in(LEDControl_a_wins));
  LED B_Wins (.in(LEDControl_b_wins));
endmodule

module RPLS (
  input  A1,
  input  A0,
  input  B1,
  input  B0,
  output W1,
  output W0
);

  wire and_1_out, and_2_out, and_3_out, and_4_out, and_5_out, and_6_out, and_7_out, and_8_out, and_9_out,
       and_10_out, not_1_out, not_2_out, not_3_out, not_4_out, or_1_out, or_3_out;

  not not_1 (not_1_out, A1);
  not not_2 (not_2_out, A0);
  not not_3 (not_3_out, B1);
  not not_4 (not_4_out, B0);
  and and_1 (and_1_out, not_2_out, not_3_out, not_4_out);
  and and_2 (and_2_out, A0, not_3_out, B0);
  and and_3 (and_3_out, not_1_out, not_2_out, B0);
  and and_4 (and_4_out, A1, A0, B1);
  and and_5 (and_5_out, A0, B1, not_4_out);
  and and_6 (and_6_out, A1, not_2_out, B1, not_4_out);
  and and_7 (and_7_out, A1, not_2_out, not_3_out, not_4_out);
  and and_8 (and_8_out, A1, A0, not_3_out, B0);
  and and_9 (and_9_out, not_1_out, not_2_out, B0);
  and and_10 (and_10_out, A0, B1, not_4_out);
  or or_1 (or_1_out, and_4_out, and_5_out, and_6_out);
  or or_2 (W1, and_7_out, and_8_out, and_9_out, and_10_out);
  or or_3 (or_3_out, and_1_out, and_2_out, and_3_out);
  or or_4 (W0, or_3_out, or_1_out);

  // Notes on the sheet:
  //   A0.B1'.B0
  //   A1'.A0'.B0
  //   A1.A0.B1
  //   A0.B1.B0'
  //   A1.A0'.B1'.B0'
  //   A1.A0.B1'.B0
  //   A1'.A0'.B0
  //   A0'.B1'.B0'
  //   A1.A0'.B1.B0'
  //   A0.B1.B0'
  //   + A1'.A0'.B0
  //   + A0.B1.B0'
  //   A0'.B1'.B0'
  //   + A0.B1'.B0
  //   + A1'.A0'.B0
  //   A1.A0.B1
  //   + A0.B1.B0'
  //   + A1.A0'.B1.B0'
  //   A1.A0'.B1'.B0'
  //   + A1.A0.B1'.B0
  //   + A0.B1'.B0
  //   + A1'.A0'.B0
  //   + A1.A0.B1
  //   + A0.B1.B0'
  //   A0'.B1'.B0'
  //   + A1.A0'.B1.B0'
endmodule

module LEDControl (
  input  W1,
  input  W0,
  output A_Wins,
  output B_Wins
);

  wire not_1_out, not_2_out;

  not not_1 (not_1_out, W0);
  not not_2 (not_2_out, W1);
  and and_1 (A_Wins, not_2_out, not_1_out);
  and and_2 (B_Wins, W1, W0);

  // Notes on the sheet:
  //   W0
  //   W0'
  //   W1
  //   W1'
endmodule
